// Logisim project decoder_i2s_v1.circ as structural Verilog: 1 circuit, main circuit main
module main (
  input  in_1
);

  wire clock_1_out, n7404_1_pin4, n7404_1_pin5, n7408_1_pin2, n7408_1_pin8, n7408_1_pin11, n7408_1_pin13,
       n7474_1_pin1, n7474_1_pin5, n7474_1_pin9, n7474_1_pin11, n7474_1_pin13, n7474_2_pin9, n7474_2_pin13,
       n7486_1_pin3, n7486_1_pin6, n74161_1_pin10, n74164_1_pin2, n74164_1_pin8, n74164_1_pin9,
       n74164_2_pin2, n74164_2_pin13;
  wire [2:0] rom_1_data;
  wire [12:0] counter_1_q;
  wire [15:0] n74164_1_pin3, register_1_q, register_2_q;

  Clock clock_1 (.out(clock_1_out));
  ROM #(.addrWidth(13), .dataWidth(3)) rom_1 (.addr(counter_1_q), .data(rom_1_data));
  Counter #(.max('h1fff), .width(13)) counter_1 (
    .Q(counter_1_q), .up(in_1), .clk(clock_1_out));  // open: load, D, count, carry, clr
  _74164 u_74164_1 (
    .pin1(rom_1_data[0]), .pin2(n74164_1_pin2), .pin3(n74164_1_pin3[0]), .pin4(n74164_1_pin3[1]),
    .pin5(n74164_1_pin3[2]), .pin6(n74164_1_pin3[3]), .pin13(n74164_1_pin3[7]), .pin12(n74164_1_pin3[6]),
    .pin11(n74164_1_pin3[5]), .pin10(n74164_1_pin3[4]), .pin9(n74164_1_pin9), .pin8(n74164_1_pin8));
  Register #(.width(16)) register_1 (.D(n74164_1_pin3), .clk(n7408_1_pin11), .Q(register_1_q));  // open: en, clr
  Register #(.width(16)) register_2 (.D(n74164_1_pin3), .clk(n7408_1_pin8), .Q(register_2_q));  // open: en, clr
  _7474 u_7474_1 (
    .pin1(n7474_1_pin1), .pin2(rom_1_data[2]), .pin3(rom_1_data[1]), .pin5(n7474_1_pin5),
    .pin13(n7474_1_pin13), .pin12(n7474_1_pin5), .pin11(n7474_1_pin11), .pin9(n7474_1_pin9));  // open: pin4, pin6, pin10, pin8
  _74164 u_74164_2 (
    .pin1(n74164_1_pin3[7]), .pin2(n74164_2_pin2), .pin3(n74164_1_pin3[8]), .pin4(n74164_1_pin3[9]),
    .pin5(n74164_1_pin3[10]), .pin6(n74164_1_pin3[11]), .pin13(n74164_2_pin13), .pin12(n74164_1_pin3[14]),
    .pin11(n74164_1_pin3[13]), .pin10(n74164_1_pin3[12]), .pin9(n74164_1_pin9), .pin8(n74164_1_pin8));
  _7474 u_7474_2 (
    .pin13(n7474_2_pin13), .pin12(n7474_1_pin9), .pin11(rom_1_data[1]), .pin9(n7474_2_pin9));  // open: pin1, pin2, pin3, pin4, pin5, pin6, pin10, pin8
  _7486 u_7486_1 (
    .pin1(n7474_2_pin9), .pin2(n7474_1_pin9), .pin3(n7486_1_pin3), .pin4(n7474_1_pin9), .pin5(n7474_1_pin5),
    .pin6(n7486_1_pin6));  // open: pin13, pin12, pin11, pin10, pin9, pin8
  _7408 u_7408_1 (
    .pin1(rom_1_data[1]), .pin2(n7408_1_pin2), .pin3(n74164_1_pin8), .pin13(n7408_1_pin13),
    .pin12(n7486_1_pin6), .pin11(n7408_1_pin11), .pin10(rom_1_data[2]), .pin9(n7486_1_pin6),
    .pin8(n7408_1_pin8));  // open: pin4, pin5, pin6
  _7404 u_7404_1 (
    .pin1(rom_1_data[1]), .pin2(n7474_1_pin11), .pin3(n7486_1_pin3), .pin4(n7404_1_pin4),
    .pin5(n7404_1_pin5), .pin6(n7408_1_pin2), .pin13(n74164_2_pin13), .pin12(n74164_1_pin3[15]),
    .pin11(rom_1_data[2]), .pin10(n7408_1_pin13));  // open: pin9, pin8
  _74161 u_74161_1 (
    .pin1(n7404_1_pin4), .pin2(rom_1_data[1]), .pin7(n7408_1_pin2), .pin15(n7404_1_pin5),
    .pin10(n74161_1_pin10), .pin9(n74161_1_pin10));  // open: pin3, pin4, pin5, pin6, pin14, pin13, pin12, pin11
  // also tied to VCC on the sheet: {n74164_1_pin2, n7474_1_pin1, n7474_1_pin13, n74164_1_pin9, n74164_2_pin2, n7474_2_pin13, n74161_1_pin10}

  // Notes on the sheet:
  //   contents of rom_1 (hex, n*v repeats v):
  //   0 2 1 3 1 3 0 2 1 3 0 2 0 2 0 2 0 2 0 2 0 2 0 2 1 3 0 2 0 2 1 3 0 2 0 2 0 2 0 2 0 2 0 2 0 2 0 2 0 2
  //   0 2 0 2 0 2 0 2 0 2 0 2 0 2 4 6 5 7 5 7 4 6 4 6 5 7 4 6 4 6 4 6 4 6 4 6 4 6 4 6 5 7 4 6 5 7 4 6 4 6
  //   4 6 4 6 4 6 4 6 4 6 4 6 4 6 4 6 4 6 4 6 4 6 4 6 4 6 4 6 0 2 1 3 1 3 0 2 1 3 0 2 0 2 0 2 0 2 0 2 0 2
  //   1 3 0 2 0 2 0 2 1 3 0 2 0 2 0 2 0 2 0 2 0 2 0 2 0 2 0 2 0 2 0 2 0 2 0 2 0 2 0 2 0 2 4 6 5 7 5 7 4 6
  //   4 6 4 6 5 7 4 6 4 6 4 6 4 6 4 6 4 6 5 7 4 6 5 7 4 6 4 6 4 6 4 6 4 6 4 6 4 6 4 6 4 6 4 6 4 6 4 6 4 6
  //   4 6 4 6 4 6 0 2 1 3 1 3 0 2 1 3 0 2 0 2 0 2 0 2 0 2 1 3 0 2 0 2 0 2 0 2 1 3 0 2 0 2 0 2 0 2 0 2 0 2
  //   0 2 0 2 0 2 0 2 0 2 0 2 0 2 0 2 0 2 0 2 4 6 5 7 5 7 4 6 4 6 4 6 4 6 5 7 4 6 4 6 4 6 4 6 4 6 5 7 4 6
  //   5 7 4 6 4 6 4 6 4 6 4 6 4 6 4 6 4 6 4 6 4 6 4 6 4 6 4 6 4 6 4 6 4 6 0 2 1 3 1 3 0 2 1 3 0 2 0 2 0 2
  //   0 2 1 3 0 2 0 2 0 2 0 2 0 2 1 3 0 2 0 2 0 2 0 2 0 2 0 2 0 2 0 2 0 2 0 2 0 2 0 2 0 2 0 2 0 2 0 2 4 6
  //   5 7 5 7 4 6 4 6 4 6 4 6 4 6 5 7 4 6 4 6 4 6 4 6 5 7 4 6 5 7 4 6 4 6 4 6 4 6 4 6 4 6 4 6 4 6 4 6 4 6
  //   4 6 4 6 4 6 4 6 4 6 4 6 0 2 1 3 1 3 0 2 1 3 0 2 0 2 0 2 1 3 0 2 0 2 0 2 0 2 0 2 0 2 1 3 0 2 0 2 0 2
  //   0 2 0 2 0 2 0 2 0 2 0 2 0 2 0 2 0 2 0 2 0 2 0 2 0 2 4 6 5 7 5 7 4 6 4 6 4 6 4 6 4 6 4 6 5 7 4 6 4 6
  //   4 6 5 7 4 6 5 7 4 6 4 6 4 6 4 6 4 6 4 6 4 6 4 6 4 6 4 6 4 6 4 6 4 6 4 6 4 6 4 6 0 2 1 3 1 3 0 2 1 3
  //   0 2 0 2 1 3 0 2 0 2 0 2 0 2 0 2 0 2 0 2 1 3 0 2 0 2 0 2 0 2 0 2 0 2 0 2 0 2 0 2 0 2 0 2 0 2 0 2 0 2
  //   0 2 0 2 4 6 5 7 5 7 4 6 4 6 4 6 4 6 4 6 4 6 4 6 5 7 4 6 4 6 5 7 4 6 5 7 4 6 4 6 4 6 4 6 4 6 4 6 4 6
  //   4 6 4 6 4 6 4 6 4 6 4 6 4 6 4 6 4 6 0 2 1 3 1 3 0 2 1 3 0 2 1 3 0 2 0 2 0 2 0 2 0 2 0 2 0 2 0 2 1 3
  //   0 2 0 2 0 2 0 2 0 2 0 2 0 2 0 2 0 2 0 2 0 2 0 2 0 2 0 2 0 2 0 2 4 6 5 7 5 7 4 6 4 6 4 6 4 6 4 6 4 6
  //   4 6 4 6 5 7 4 6 5 7 4 6 5 7 4 6 4 6 4 6 4 6 4 6 4 6 4 6 4 6 4 6 4 6 4 6 4 6 4 6 4 6 4 6 4 6 0 2 1 3
  //   1 3 0 2 1 3 1 3 0 2 0 2 0 2 0 2 0 2 0 2 0 2 0 2 0 2 1 3 0 2 0 2 0 2 0 2 0 2 0 2 0 2 0 2 0 2 0 2 0 2
  //   0 2 0 2 0 2 0 2 0 2 4 6 5 7 5 7 4 6 4 6 4 6 4 6 4 6 4 6 4 6 4 6 4 6 5 7 5 7 4 6 5 7 4 6 4 6 4 6 4 6
  //   4 6 4 6 4 6 4 6 4 6 4 6 4 6 4 6 4 6 4 6 4 6 4 6 0 2 1 3 1 3 0 2 1 3 0 2 0 2 0 2 0 2 0 2 0 2 0 2 1 3
  //   0 2 0 2 1 3 0 2 0 2 0 2 0 2 0 2 0 2 0 2 0 2 0 2 0 2 0 2 0 2 0 2 0 2 0 2 0 2 4 6 5 7 5 7 4 6 4 6 5 7
  //   4 6 4 6 4 6 4 6 4 6 4 6 4 6 5 7 4 6 5 7 4 6 4 6 4 6 4 6 4 6 4 6 4 6 4 6 4 6 4 6 4 6 4 6 4 6 4 6 4 6
  //   4 6 0 2 1 3 1 3 0 2 1 3 0 2 0 2 0 2 0 2 0 2 0 2 1 3 0 2 0 2 0 2 1 3 0 2 0 2 0 2 0 2 0 2 0 2 0 2 0 2
  //   0 2 0 2 0 2 0 2 0 2 0 2 0 2 0 2 4 6 5 7 5 7 4 6 4 6 4 6 5 7 4 6 4 6 4 6 4 6 4 6 4 6 5 7 4 6 5 7 4 6
  //   4 6 4 6 4 6 4 6 4 6 4 6 4 6 4 6 4 6 4 6 4 6 4 6 4 6 4 6 4 6 0 2 1 3 1 3 0 2 1 3 0 2 0 2 0 2 0 2 0 2
  //   1 3 0 2 0 2 0 2 0 2 1 3 0 2 0 2 0 2 0 2 0 2 0 2 0 2 0 2 0 2 0 2 0 2 0 2 0 2 0 2 0 2 0 2 4 6 5 7 5 7
  //   4 6 4 6 4 6 4 6 5 7 4 6 4 6 4 6 4 6 4 6 5 7 4 6 5 7 4 6 4 6 4 6 4 6 4 6 4 6 4 6 4 6 4 6 4 6 4 6 4 6
  //   4 6 4 6 4 6 4 6 0 2 1 3 1 3 0 2 1 3 0 2 0 2 0 2 0 2 1 3 0 2 0 2 0 2 0 2 0 2 1 3 0 2 0 2 0 2 0 2 0 2
  //   0 2 0 2 0 2 0 2 0 2 0 2 0 2 0 2 0 2 0 2 0 2 4 6 5 7 5 7 4 6 4 6 4 6 4 6 4 6 5 7 4 6 4 6 4 6 4 6 5 7
  //   4 6 5 7 4 6 4 6 4 6 4 6 4 6 4 6 4 6 4 6 4 6 4 6 4 6 4 6 4 6 4 6 4 6 4 6 0 2 1 3 1 3 0 2 1 3 0 2 0 2
  //   0 2 1 3 0 2 0 2 0 2 0 2 0 2 0 2 1 3 0 2 0 2 0 2 0 2 0 2 0 2 0 2 0 2 0 2 0 2 0 2 0 2 0 2 0 2 0 2 0 2
  //   4 6 5 7 5 7 4 6 4 6 4 6 4 6 4 6 4 6 5 7 4 6 4 6 4 6 5 7 4 6 5 7 4 6 4 6 4 6 4 6 4 6 4 6 4 6 4 6 4 6
  //   4 6 4 6 4 6 4 6 4 6 4 6 4 6 0 2 1 3 1 3 0 2 1 3 0 2 0 2 1 3 0 2 0 2 0 2 0 2 0 2 0 2 0 2 1 3 0 2 0 2
  //   0 2 0 2 0 2 0 2 0 2 0 2 0 2 0 2 0 2 0 2 0 2 0 2 0 2 0 2 4 6 5 7 5 7 4 6 4 6 4 6 4 6 4 6 4 6 4 6 5 7
  //   4 6 4 6 5 7 4 6 5 7 4 6 4 6 4 6 4 6 4 6 4 6 4 6 4 6 4 6 4 6 4 6 4 6 4 6 4 6 4 6 4 6 0 2 1 3 1 3 0 2
  //   1 3 0 2 1 3 0 2 0 2 0 2 0 2 0 2 0 2 0 2 0 2 1 3 0 2 0 2 0 2 0 2 0 2 0 2 0 2 0 2 0 2 0 2 0 2 0 2 0 2
  //   0 2 0 2 0 2 4 6 5 7 5 7 4 6 4 6 4 6 4 6 4 6 4 6 4 6 4 6 5 7 4 6 5 7 4 6 5 7 4 6 4 6 4 6 4 6 4 6 4 6
  //   4 6 4 6 4 6 4 6 4 6 4 6 4 6 4 6 4 6 4 6 0 2 1 3 1 3 0 2 1 3 1 3 0 2 0 2 0 2 0 2 0 2 0 2 0 2 0 2 0 2
  //   1 3 0 2 0 2 0 2 0 2 0 2 0 2 0 2 0 2 0 2 0 2 0 2 0 2 0 2 0 2 0 2 0 2 4 6 5 7 5 7 4 6 4 6 4 6 4 6 4 6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
endmodule
