// Logisim project decoder_i2s_v2_1.circ as structural Verilog: 1 circuit, main circuit main
module main (
);

  wire clock_1_out, n7404_1_pin2, n7404_1_pin4, n7404_1_pin9, n7408_1_pin3, n7408_1_pin6, n7474_1_pin1,
       n7474_1_pin5, n74164_1_pin2, n74164_1_pin3, n74164_1_pin4, n74164_1_pin5, n74164_1_pin6,
       n74164_1_pin13, n74164_2_pin3, n74164_2_pin4, n74164_2_pin5, n74164_2_pin6;
  wire [2:0] rom_1_data;
  wire [12:0] counter_1_q;
  wire [15:0] n74164_2_pin13, register_1_q, register_2_q;

  Clock clock_1 (.out(clock_1_out));
  ROM #(.addrWidth(13), .dataWidth(3)) rom_1 (.addr(counter_1_q), .data(rom_1_data));
  Counter #(.max('h1fff), .width(13)) counter_1 (
    .Q(counter_1_q), .clk(clock_1_out));  // open: load, D, count, carry, up, clr
  _74164 u_74164_1 (
    .pin1(rom_1_data[0]), .pin2(n74164_1_pin2), .pin3(n74164_1_pin3), .pin4(n74164_1_pin4),
    .pin5(n74164_1_pin5), .pin6(n74164_1_pin6), .pin13(n74164_1_pin13), .pin8(rom_1_data[1]));  // open: pin12, pin11, pin10, pin9
  _7474 u_7474_1 (
    .pin1(n7474_1_pin1), .pin2(rom_1_data[2]), .pin3(rom_1_data[1]), .pin5(n7474_1_pin5));  // open: pin4, pin6, pin13, pin12, pin11, pin10, pin9, pin8
  _74164 u_74164_2 (
    .pin1(n74164_1_pin13), .pin2(n74164_1_pin2), .pin3(n74164_2_pin3), .pin4(n74164_2_pin4),
    .pin5(n74164_2_pin5), .pin6(n74164_2_pin6), .pin13(n74164_2_pin13[0]), .pin8(rom_1_data[1]));  // open: pin12, pin11, pin10, pin9
  _7404 u_7404_1 (
    .pin1(rom_1_data[2]), .pin2(n7404_1_pin2), .pin3(n7474_1_pin5), .pin4(n7404_1_pin4), .pin9(n7404_1_pin9),
    .pin8(n74164_2_pin13[15]));  // open: pin5, pin6, pin13, pin12, pin11, pin10
  _74164 u_74164_3 (
    .pin1(n74164_2_pin13[0]), .pin2(n74164_1_pin2), .pin3(n74164_2_pin13[1]), .pin4(n74164_2_pin13[2]),
    .pin5(n74164_2_pin13[3]), .pin6(n74164_2_pin13[4]), .pin13(n74164_2_pin13[8]), .pin12(n74164_2_pin13[7]),
    .pin11(n74164_2_pin13[6]), .pin10(n74164_2_pin13[5]), .pin8(rom_1_data[1]));  // open: pin9
  _7408 u_7408_1 (
    .pin1(n7474_1_pin5), .pin2(n7404_1_pin2), .pin3(n7408_1_pin3), .pin4(rom_1_data[2]), .pin5(n7404_1_pin4),
    .pin6(n7408_1_pin6));  // open: pin13, pin12, pin11, pin10, pin9, pin8
  _74164 u_74164_4 (
    .pin1(n74164_2_pin13[8]), .pin2(n74164_1_pin2), .pin3(n74164_2_pin13[9]), .pin4(n74164_2_pin13[10]),
    .pin5(n74164_2_pin13[11]), .pin6(n74164_2_pin13[12]), .pin12(n7404_1_pin9), .pin11(n74164_2_pin13[14]),
    .pin10(n74164_2_pin13[13]), .pin8(rom_1_data[1]));  // open: pin13, pin9
  Register #(.width(16)) register_1 (.D(n74164_2_pin13), .clk(n7408_1_pin6), .Q(register_1_q));  // open: en, clr
  Register #(.width(16)) register_2 (.D(n74164_2_pin13), .clk(n7408_1_pin3), .Q(register_2_q));  // open: en, clr
  // Digital_Oscilloscope digital_oscilloscope_1: pin names not known; wires that end beside it: rom_1_data[1], n7408_1_pin3, n7408_1_pin6, n74164_2_pin13[1]
  // also tied to VCC on the sheet: {n7474_1_pin1, n74164_1_pin2}

  // Notes on the sheet:
  //   contents of rom_1 (hex, n*v repeats v):
  //   0 2 1 3 1 3 0 2 1 3 0 2 0 2 0 2 0 2 0 2 0 2 0 2 1 3 0 2 0 2 1 3 0 2 0 2 0 2 0 2 0 2 0 2 0 2 0 2 0 2
  //   0 2 0 2 0 2 0 2 0 2 0 2 0 2 4 6 5 7 5 7 4 6 4 6 5 7 4 6 4 6 4 6 4 6 4 6 4 6 4 6 5 7 4 6 5 7 4 6 4 6
  //   4 6 4 6 4 6 4 6 4 6 4 6 4 6 4 6 4 6 4 6 4 6 4 6 4 6 4 6 0 2 1 3 1 3 0 2 1 3 0 2 0 2 0 2 0 2 0 2 0 2
  //   1 3 0 2 0 2 0 2 1 3 0 2 0 2 0 2 0 2 0 2 0 2 0 2 0 2 0 2 0 2 0 2 0 2 0 2 0 2 0 2 0 2 4 6 5 7 5 7 4 6
  //   4 6 4 6 5 7 4 6 4 6 4 6 4 6 4 6 4 6 5 7 4 6 5 7 4 6 4 6 4 6 4 6 4 6 4 6 4 6 4 6 4 6 4 6 4 6 4 6 4 6
  //   4 6 4 6 4 6 0 2 1 3 1 3 0 2 1 3 0 2 0 2 0 2 0 2 0 2 1 3 0 2 0 2 0 2 0 2 1 3 0 2 0 2 0 2 0 2 0 2 0 2
  //   0 2 0 2 0 2 0 2 0 2 0 2 0 2 0 2 0 2 0 2 4 6 5 7 5 7 4 6 4 6 4 6 4 6 5 7 4 6 4 6 4 6 4 6 4 6 5 7 4 6
  //   5 7 4 6 4 6 4 6 4 6 4 6 4 6 4 6 4 6 4 6 4 6 4 6 4 6 4 6 4 6 4 6 4 6 0 2 1 3 1 3 0 2 1 3 0 2 0 2 0 2
  //   0 2 1 3 0 2 0 2 0 2 0 2 0 2 1 3 0 2 0 2 0 2 0 2 0 2 0 2 0 2 0 2 0 2 0 2 0 2 0 2 0 2 0 2 0 2 0 2 4 6
  //   5 7 5 7 4 6 4 6 4 6 4 6 4 6 5 7 4 6 4 6 4 6 4 6 5 7 4 6 5 7 4 6 4 6 4 6 4 6 4 6 4 6 4 6 4 6 4 6 4 6
  //   4 6 4 6 4 6 4 6 4 6 4 6 0 2 1 3 1 3 0 2 1 3 0 2 0 2 0 2 1 3 0 2 0 2 0 2 0 2 0 2 0 2 1 3 0 2 0 2 0 2
  //   0 2 0 2 0 2 0 2 0 2 0 2 0 2 0 2 0 2 0 2 0 2 0 2 0 2 4 6 5 7 5 7 4 6 4 6 4 6 4 6 4 6 4 6 5 7 4 6 4 6
  //   4 6 5 7 4 6 5 7 4 6 4 6 4 6 4 6 4 6 4 6 4 6 4 6 4 6 4 6 4 6 4 6 4 6 4 6 4 6 4 6 0 2 1 3 1 3 0 2 1 3
  //   0 2 0 2 1 3 0 2 0 2 0 2 0 2 0 2 0 2 0 2 1 3 0 2 0 2 0 2 0 2 0 2 0 2 0 2 0 2 0 2 0 2 0 2 0 2 0 2 0 2
  //   0 2 0 2 4 6 5 7 5 7 4 6 4 6 4 6 4 6 4 6 4 6 4 6 5 7 4 6 4 6 5 7 4 6 5 7 4 6 4 6 4 6 4 6 4 6 4 6 4 6
  //   4 6 4 6 4 6 4 6 4 6 4 6 4 6 4 6 4 6 0 2 1 3 1 3 0 2 1 3 0 2 1 3 0 2 0 2 0 2 0 2 0 2 0 2 0 2 0 2 1 3
  //   0 2 0 2 0 2 0 2 0 2 0 2 0 2 0 2 0 2 0 2 0 2 0 2 0 2 0 2 0 2 0 2 4 6 5 7 5 7 4 6 4 6 4 6 4 6 4 6 4 6
  //   4 6 4 6 5 7 4 6 5 7 4 6 5 7 4 6 4 6 4 6 4 6 4 6 4 6 4 6 4 6 4 6 4 6 4 6 4 6 4 6 4 6 4 6 4 6 0 2 1 3
  //   1 3 0 2 1 3 1 3 0 2 0 2 0 2 0 2 0 2 0 2 0 2 0 2 0 2 1 3 0 2 0 2 0 2 0 2 0 2 0 2 0 2 0 2 0 2 0 2 0 2
  //   0 2 0 2 0 2 0 2 0 2 4 6 5 7 5 7 4 6 4 6 4 6 4 6 4 6 4 6 4 6 4 6 4 6 5 7 5 7 4 6 5 7 4 6 4 6 4 6 4 6
  //   4 6 4 6 4 6 4 6 4 6 4 6 4 6 4 6 4 6 4 6 4 6 4 6 0 2 1 3 1 3 0 2 1 3 0 2 0 2 0 2 0 2 0 2 0 2 0 2 1 3
  //   0 2 0 2 1 3 0 2 0 2 0 2 0 2 0 2 0 2 0 2 0 2 0 2 0 2 0 2 0 2 0 2 0 2 0 2 0 2 4 6 5 7 5 7 4 6 4 6 5 7
  //   4 6 4 6 4 6 4 6 4 6 4 6 4 6 5 7 4 6 5 7 4 6 4 6 4 6 4 6 4 6 4 6 4 6 4 6 4 6 4 6 4 6 4 6 4 6 4 6 4 6
  //   4 6 0 2 1 3 1 3 0 2 1 3 0 2 0 2 0 2 0 2 0 2 0 2 1 3 0 2 0 2 0 2 1 3 0 2 0 2 0 2 0 2 0 2 0 2 0 2 0 2
  //   0 2 0 2 0 2 0 2 0 2 0 2 0 2 0 2 4 6 5 7 5 7 4 6 4 6 4 6 5 7 4 6 4 6 4 6 4 6 4 6 4 6 5 7 4 6 5 7 4 6
  //   4 6 4 6 4 6 4 6 4 6 4 6 4 6 4 6 4 6 4 6 4 6 4 6 4 6 4 6 4 6 0 2 1 3 1 3 0 2 1 3 0 2 0 2 0 2 0 2 0 2
  //   1 3 0 2 0 2 0 2 0 2 1 3 0 2 0 2 0 2 0 2 0 2 0 2 0 2 0 2 0 2 0 2 0 2 0 2 0 2 0 2 0 2 0 2 4 6 5 7 5 7
  //   4 6 4 6 4 6 4 6 5 7 4 6 4 6 4 6 4 6 4 6 5 7 4 6 5 7 4 6 4 6 4 6 4 6 4 6 4 6 4 6 4 6 4 6 4 6 4 6 4 6
  //   4 6 4 6 4 6 4 6 0 2 1 3 1 3 0 2 1 3 0 2 0 2 0 2 0 2 1 3 0 2 0 2 0 2 0 2 0 2 1 3 0 2 0 2 0 2 0 2 0 2
  //   0 2 0 2 0 2 0 2 0 2 0 2 0 2 0 2 0 2 0 2 0 2 4 6 5 7 5 7 4 6 4 6 4 6 4 6 4 6 5 7 4 6 4 6 4 6 4 6 5 7
  //   4 6 5 7 4 6 4 6 4 6 4 6 4 6 4 6 4 6 4 6 4 6 4 6 4 6 4 6 4 6 4 6 4 6 4 6 0 2 1 3 1 3 0 2 1 3 0 2 0 2
  //   0 2 1 3 0 2 0 2 0 2 0 2 0 2 0 2 1 3 0 2 0 2 0 2 0 2 0 2 0 2 0 2 0 2 0 2 0 2 0 2 0 2 0 2 0 2 0 2 0 2
  //   4 6 5 7 5 7 4 6 4 6 4 6 4 6 4 6 4 6 5 7 4 6 4 6 4 6 5 7 4 6 5 7 4 6 4 6 4 6 4 6 4 6 4 6 4 6 4 6 4 6
  //   4 6 4 6 4 6 4 6 4 6 4 6 4 6 0 2 1 3 1 3 0 2 1 3 0 2 0 2 1 3 0 2 0 2 0 2 0 2 0 2 0 2 0 2 1 3 0 2 0 2
  //   0 2 0 2 0 2 0 2 0 2 0 2 0 2 0 2 0 2 0 2 0 2 0 2 0 2 0 2 4 6 5 7 5 7 4 6 4 6 4 6 4 6 4 6 4 6 4 6 5 7
  //   4 6 4 6 5 7 4 6 5 7 4 6 4 6 4 6 4 6 4 6 4 6 4 6 4 6 4 6 4 6 4 6 4 6 4 6 4 6 4 6 4 6 0 2 1 3 1 3 0 2
  //   1 3 0 2 1 3 0 2 0 2 0 2 0 2 0 2 0 2 0 2 0 2 1 3 0 2 0 2 0 2 0 2 0 2 0 2 0 2 0 2 0 2 0 2 0 2 0 2 0 2
  //   0 2 0 2 0 2 4 6 5 7 5 7 4 6 4 6 4 6 4 6 4 6 4 6 4 6 4 6 5 7 4 6 5 7 4 6 5 7 4 6 4 6 4 6 4 6 4 6 4 6
  //   4 6 4 6 4 6 4 6 4 6 4 6 4 6 4 6 4 6 4 6 0 2 1 3 1 3 0 2 1 3 1 3 0 2 0 2 0 2 0 2 0 2 0 2 0 2 0 2 0 2
  //   1 3 0 2 0 2 0 2 0 2 0 2 0 2 0 2 0 2 0 2 0 2 0 2 0 2 0 2 0 2 0 2 0 2 4 6 5 7 5 7 4 6 4 6 4 6 4 6 4 6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
endmodule
